# Fritzing sketch CeilingFan (saved by Fritzing 0.9.9b)
circuit board: 15.8891cm x 8.04337cm
breadboards: 1

parts:
  PCA9685 = PCA9685 16x12-bit PWM Breakout
  Relay_module = Module 4 Relais 5V [package="Module 4 Relais 5V"]
  J1 = female pin header, 15 pins [form="♀ (female)"]
  J2 = female pin header, 15 pins [form="♀ (female)"]
  ESP8266 = Amica NodeMCU DEVKIT 1.0

nets:
  N1: PCA9685.no_name_yet#501, PCA9685.no_name_yet#1000, Relay_module.GND, J1.pin7, J1.pin14, J2.pin10, J2.pin14, ESP8266.pin2, ESP8266.pin_9, ESP8266.pin_25, ESP8266.pin_29
  N2: PCA9685.no_name_yet#503, J1.pin2, ESP8266.pin_14
  N3: PCA9685.no_name_yet#504, J1.pin3, ESP8266.pin_13
  N4: PCA9685.no_name_yet#505, J1.pin6, J1.pin15, J2.pin11, ESP8266.pin1, ESP8266.pin_10, ESP8266.pin_26
  N5: Relay_module.VCC, J2.pin15, ESP8266.pin_30
  N6: Relay_module.IN1, J1.pin9, ESP8266.pin7
  N7: Relay_module.IN2, J1.pin10, ESP8266.pin6
  N8: Relay_module.IN3, J1.pin8, ESP8266.pin8
  N9: Relay_module.IN4, J1.pin11, ESP8266.pin5
  N10: J1.pin1, ESP8266.pin_15
  N11: J1.pin4, ESP8266.pin_12
  N12: J1.pin5, ESP8266.pin_11
  N13: J1.pin12, ESP8266.pin4
  N14: J1.pin13, ESP8266.pin3
  N15: J2.pin1, ESP8266.pin_16
  N16: J2.pin2, ESP8266.pin_17
  N17: J2.pin3, ESP8266.pin_18
  N18: J2.pin4, ESP8266.pin_19
  N19: J2.pin5, ESP8266.pin_20
  N20: J2.pin6, ESP8266.pin_21
  N21: J2.pin7, ESP8266.pin_22
  N22: J2.pin8, ESP8266.pin_23
  N23: J2.pin9, ESP8266.pin_24
  N24: J2.pin12, ESP8266.pin_27
  N25: J2.pin13, ESP8266.pin_28

custom parts:
  Module 4 Relais 5V: Module 4 Relais 5V 4x SPD-06VDC-SD-C
  Amica NodeMCU DEVKIT 1.0: Amica NodeMCU DEVKIT 1.0 Development Kit based on ESP8266 ESP-12E, integating GPIO, PWM, IIC, 1-Wire and ADC all in one board. Links: NodeMCU information page Github
